# Fritzing sketch v1 (saved by Fritzing 0.9.5d)
breadboards: 1

parts:
  S1 = Pushbutton [package="[SMD]"]
  Part1 = Arduino Uno (Rev3) - ICSP
  LED1 = RGB LED - (4 legs) [package="5 mm [THT]"]
  R1 = Resistor [tolerance=±5% resistance=220 package=THT]

nets:
  N1: S1.Pin_1, S1.Pin_2, R1.Pin_0
  N2: S1.Pin_3, S1.Pin_4, Part1.D12/MISO, Part1.5V, LED1.common_anode
  N3: Part1.D3_PWM, LED1.red_cathode
  N4: Part1.D5_PWM, LED1.green_cathode
  N5: Part1.D6_PWM, LED1.blue_cathode
  N6: Part1.GND, R1.Pin_1
